// Logisim project fullhaderrr.circ as structural Verilog: 3 circuits, main circuit main
module main (
  input  in_1,
  input  in_2,
  input  b0,
  input  a0,
  output out_5,
  output out_6
);

  fullhader fullhader_1 ();  // open: cin, A, B, s, cot
  fullhader fullhader_2 ();  // open: cin, A, B, s, cot
  fullhader fullhader_3 (.A(in_2), .B(in_1), .s(out_6));  // open: cin, cot
  fullhader fullhader_4 (.A(b0), .B(a0), .cot(out_5));  // open: cin, s
endmodule

module halfader (
  input  A,
  input  B,
  output S,
  output C
);

  xor xor_1 (S, A, A);
  and and_1 (C, A, A);

  assign B = A;
endmodule

module fullhader (
  input  cin,
  input  A,
  input  B,
  output s,
  output cot
);

  wire halfader_1_c, halfader_1_s, halfader_2_c;

  halfader halfader_1 (.A(A), .B(B), .S(halfader_1_s), .C(halfader_1_c));
  halfader halfader_2 (.A(cin), .B(halfader_1_s), .S(s), .C(halfader_2_c));
  or or_1 (cot, halfader_2_c, halfader_1_c);
endmodule
